// Logisim project EP01_EP02_pt1.circ as structural Verilog: 9 circuits, main circuit meio_Somador
module meio_Somador (
  input  X0,
  input  Y0,
  output S0,
  output Vai1
);

  and and_1 (Vai1, X0, Y0);
  xor xor_1 (S0, X0, Y0);

  // Notes on the sheet:
  //   ALUNO: Arthur de Sá Braz de Matos
  //   MATRÍCULA: 801778
endmodule

module somadorCompleto2Bits (
  input  X,
  input  Vem1,
  input  Y,
  output S,
  output Vai1
);

  wire meio_somador_1_s0, meio_somador_1_vai1, meio_somador_2_vai1;

  meio_Somador meio_somador_1 (.X0(X), .Y0(Y), .Vai1(meio_somador_1_vai1), .S0(meio_somador_1_s0));
  or or_1 (Vai1, meio_somador_1_vai1, meio_somador_2_vai1);
  meio_Somador meio_somador_2 (.X0(Vem1), .Y0(meio_somador_1_s0), .Vai1(meio_somador_2_vai1), .S0(S));

  // Notes on the sheet:
  //   MATRÍCULA: 801778
  //   ALUNO: Arthur de Sá Braz de Matos
endmodule

module somadorCompleto4Bits (
  input  x3,
  input  x2,
  input  x1,
  input  x0,
  input  y3,
  input  y2,
  input  y1,
  input  y0,
  input  P_Vai1,
  output OF,
  output s3,
  output s2,
  output s1,
  output s0
);

  wire somadorcompleto2bits_2_vai1, somadorcompleto2bits_3_vai1, somadorcompleto2bits_4_vai1;

  somadorCompleto2Bits somadorcompleto2bits_1 (.X(x3), .Vem1(somadorcompleto2bits_2_vai1), .Y(y3), .Vai1(OF), .S(s3));
  somadorCompleto2Bits somadorcompleto2bits_2 (
    .X(x2), .Vem1(somadorcompleto2bits_3_vai1), .Y(y2), .Vai1(somadorcompleto2bits_2_vai1), .S(s2));
  somadorCompleto2Bits somadorcompleto2bits_3 (
    .X(x1), .Vem1(somadorcompleto2bits_4_vai1), .Y(y1), .Vai1(somadorcompleto2bits_3_vai1), .S(s1));
  somadorCompleto2Bits somadorcompleto2bits_4 (
    .X(x0), .Vem1(P_Vai1), .Y(y0), .Vai1(somadorcompleto2bits_4_vai1), .S(s0));

  // Notes on the sheet:
  //   ALUNO: Arthur de Sá Braz de Matos
  //   MATRÍCULA: 801778
  //   Primeiro Vai1 = 0
endmodule

module decodificador_Hexa (
  input  e3,
  input  e2,
  input  e1,
  input  e0,
  output a,
  output b,
  output c,
  output d,
  output e,
  output f,
  output g
);

  wire and_1_out, and_2_out, and_3_out, and_4_out, and_5_out, and_6_out, and_7_out, and_8_out, and_9_out,
       and_10_out, and_11_out, and_12_out, and_13_out, and_14_out, and_15_out, and_16_out, and_17_out,
       and_18_out, and_19_out, and_20_out, and_21_out, and_22_out, and_23_out, and_24_out, and_25_out,
       and_26_out, and_27_out, and_28_out, and_29_out, and_30_out, and_31_out, and_32_out, and_33_out,
       and_34_out, and_35_out, not_1_out, not_2_out, not_3_out, not_4_out, not_5_out, not_6_out, not_7_out,
       not_8_out, not_9_out, not_10_out, not_11_out, not_12_out, not_13_out, not_14_out, not_15_out,
       not_16_out, not_17_out, not_18_out, not_19_out, not_20_out, not_21_out, not_22_out, not_23_out,
       not_24_out, not_25_out, not_26_out, not_27_out, not_28_out, not_29_out, not_30_out, not_31_out,
       not_32_out, not_33_out, not_34_out, not_35_out, not_36_out, not_37_out, not_38_out, not_39_out,
       not_40_out, not_41_out, not_42_out, not_43_out;

  not not_1 (not_1_out, e2);
  and and_1 (and_1_out, not_1_out, not_2_out);
  not not_2 (not_2_out, e0);
  not not_3 (not_3_out, e3);
  and and_2 (and_2_out, not_3_out, e1);
  not not_4 (not_4_out, e3);
  and and_3 (and_3_out, not_4_out, e2, e0);
  and and_4 (and_4_out, e2, e1);
  not not_5 (not_5_out, e2);
  and and_5 (and_5_out, e3, not_5_out, not_6_out);
  not not_6 (not_6_out, e1);
  and and_6 (and_6_out, e3, not_7_out);
  not not_7 (not_7_out, e0);
  not not_8 (not_8_out, e3);
  and and_7 (and_7_out, not_8_out, not_9_out);
  not not_9 (not_9_out, e2);
  not not_10 (not_10_out, e3);
  not not_11 (not_11_out, e1);
  and and_8 (and_8_out, not_10_out, not_11_out, not_12_out);
  not not_12 (not_12_out, e0);
  not not_13 (not_13_out, e2);
  and and_9 (and_9_out, not_13_out, not_14_out);
  not not_14 (not_14_out, e0);
  not not_15 (not_15_out, e3);
  and and_10 (and_10_out, not_15_out, e1, e0);
  not not_16 (not_16_out, e1);
  and and_11 (and_11_out, e3, not_16_out, e0);
  not not_17 (not_17_out, e3);
  and and_12 (and_12_out, not_17_out, not_18_out);
  not not_18 (not_18_out, e1);
  not not_19 (not_19_out, e3);
  and and_13 (and_13_out, not_19_out, e0);
  not not_20 (not_20_out, e1);
  and and_14 (and_14_out, not_20_out, e0);
  not not_21 (not_21_out, e3);
  and and_15 (and_15_out, not_21_out, e2);
  and and_16 (and_16_out, e3, not_22_out);
  not not_22 (not_22_out, e2);
  not not_23 (not_23_out, e3);
  and and_17 (and_17_out, not_23_out, not_24_out, not_25_out);
  not not_24 (not_24_out, e2);
  not not_25 (not_25_out, e0);
  not not_26 (not_26_out, e2);
  and and_18 (and_18_out, not_26_out, e1, e0);
  not not_27 (not_27_out, e1);
  and and_19 (and_19_out, e2, not_27_out, e0);
  and and_20 (and_20_out, e2, e1, not_28_out);
  not not_28 (not_28_out, e0);
  and and_21 (and_21_out, e3, not_29_out);
  not not_29 (not_29_out, e1);
  not not_30 (not_30_out, e2);
  and and_22 (and_22_out, not_30_out, not_31_out);
  not not_31 (not_31_out, e0);
  and and_23 (and_23_out, e1, not_32_out);
  not not_32 (not_32_out, e0);
  and and_24 (and_24_out, e3, e1);
  and and_25 (and_25_out, e3, e2);
  not not_33 (not_33_out, e1);
  and and_26 (and_26_out, not_33_out, not_34_out);
  not not_34 (not_34_out, e0);
  not not_35 (not_35_out, e3);
  and and_27 (and_27_out, not_35_out, e2, not_36_out);
  not not_36 (not_36_out, e1);
  and and_28 (and_28_out, e2, not_37_out);
  not not_37 (not_37_out, e0);
  and and_29 (and_29_out, e3, not_38_out);
  not not_38 (not_38_out, e2);
  and and_30 (and_30_out, e3, e1);
  not not_39 (not_39_out, e2);
  and and_31 (and_31_out, not_39_out, e1);
  and and_32 (and_32_out, e1, not_40_out);
  not not_40 (not_40_out, e0);
  not not_41 (not_41_out, e3);
  and and_33 (and_33_out, not_41_out, e2, not_42_out);
  not not_42 (not_42_out, e1);
  and and_34 (and_34_out, e3, not_43_out);
  not not_43 (not_43_out, e2);
  and and_35 (and_35_out, e3, e0);
  or or_1 (b, and_7_out, and_8_out, and_9_out, and_10_out, and_11_out);
  or or_2 (c, and_12_out, and_13_out, and_14_out, and_15_out, and_16_out);
  or or_3 (d, and_17_out, and_18_out, and_19_out, and_20_out, and_21_out);
  or or_4 (e, and_22_out, and_23_out, and_24_out, and_25_out);
  or or_5 (f, and_26_out, and_27_out, and_28_out, and_29_out, and_30_out);
  or or_6 (g, and_31_out, and_32_out, and_33_out, and_34_out, and_35_out);
  or or_7 (a, and_1_out, and_2_out, and_3_out, and_4_out, and_5_out, and_6_out);

  // Notes on the sheet:
  //   MATRÍCULA: 801778
  //   ALUNO: Arthur de Sá Braz de Matos
endmodule

module display (
  input  a,
  input  b,
  input  c,
  input  d
);

  wire decodificador_hexa_1_a, decodificador_hexa_1_b, decodificador_hexa_1_c, decodificador_hexa_1_d,
       decodificador_hexa_1_e, decodificador_hexa_1_f, decodificador_hexa_1_g;

  decodificador_Hexa decodificador_hexa_1 (
    .e3(a), .e2(b), .e1(c), .e0(d), .a(decodificador_hexa_1_a), .b(decodificador_hexa_1_b),
    .c(decodificador_hexa_1_c), .d(decodificador_hexa_1_d), .e(decodificador_hexa_1_e),
    .f(decodificador_hexa_1_f), .g(decodificador_hexa_1_g));
  _7_Segment_Display u_7_segment_display_1 (
    .g(decodificador_hexa_1_g), .f(decodificador_hexa_1_f), .a(decodificador_hexa_1_a),
    .b(decodificador_hexa_1_b), .e(decodificador_hexa_1_e), .d(decodificador_hexa_1_d),
    .c(decodificador_hexa_1_c));  // open: dp

  // Notes on the sheet:
  //   ALUNO: Arthur de Sá Braz de Matos
  //   MATRÍCULA: 801778
endmodule

module calculadora (
  input  Y0,
  input  Y1,
  input  Y2,
  input  C_in,
  input  Y3,
  input  X0,
  input  X1,
  input  X2,
  input  X3,
  output S3,
  output S2,
  output S1,
  output S0,
  output OF
);

  wire decodificador_hexa_1_a, decodificador_hexa_1_b, decodificador_hexa_1_c, decodificador_hexa_1_d,
       decodificador_hexa_1_e, decodificador_hexa_1_f, decodificador_hexa_1_g, decodificador_hexa_2_a,
       decodificador_hexa_2_b, decodificador_hexa_2_c, decodificador_hexa_2_d, decodificador_hexa_2_e,
       decodificador_hexa_2_f, decodificador_hexa_2_g, decodificador_hexa_3_a, decodificador_hexa_3_b,
       decodificador_hexa_3_c, decodificador_hexa_3_d, decodificador_hexa_3_e, decodificador_hexa_3_f,
       decodificador_hexa_3_g;

  somadorCompleto4Bits somadorcompleto4bits_1 (
    .x3(X3), .x2(X2), .x1(X1), .x0(X0), .y3(Y3), .y2(Y2), .y1(Y1), .y0(Y0), .OF(OF), .s3(S3), .s2(S2),
    .s1(S1), .s0(S0), .P_Vai1(C_in));
  decodificador_Hexa decodificador_hexa_1 (
    .e3(Y3), .e2(Y2), .e1(Y1), .e0(Y0), .a(decodificador_hexa_1_a), .b(decodificador_hexa_1_b),
    .c(decodificador_hexa_1_c), .d(decodificador_hexa_1_d), .e(decodificador_hexa_1_e),
    .f(decodificador_hexa_1_f), .g(decodificador_hexa_1_g));
  decodificador_Hexa decodificador_hexa_2 (
    .e3(X3), .e2(X2), .e1(X1), .e0(X0), .a(decodificador_hexa_2_a), .b(decodificador_hexa_2_b),
    .c(decodificador_hexa_2_c), .d(decodificador_hexa_2_d), .e(decodificador_hexa_2_e),
    .f(decodificador_hexa_2_f), .g(decodificador_hexa_2_g));
  _7_Segment_Display u_7_segment_display_1 (
    .g(decodificador_hexa_1_g), .f(decodificador_hexa_1_f), .a(decodificador_hexa_1_a),
    .b(decodificador_hexa_1_b), .e(decodificador_hexa_1_e), .d(decodificador_hexa_1_d),
    .c(decodificador_hexa_1_c));  // open: dp
  _7_Segment_Display u_7_segment_display_2 (
    .g(decodificador_hexa_2_g), .f(decodificador_hexa_2_f), .a(decodificador_hexa_2_a),
    .b(decodificador_hexa_2_b), .e(decodificador_hexa_2_e), .d(decodificador_hexa_2_d),
    .c(decodificador_hexa_2_c));  // open: dp
  decodificador_Hexa decodificador_hexa_3 (
    .e3(S3), .e2(S2), .e1(S1), .e0(S0), .a(decodificador_hexa_3_a), .b(decodificador_hexa_3_b),
    .c(decodificador_hexa_3_c), .d(decodificador_hexa_3_d), .e(decodificador_hexa_3_e),
    .f(decodificador_hexa_3_f), .g(decodificador_hexa_3_g));
  _7_Segment_Display u_7_segment_display_3 (
    .g(decodificador_hexa_3_g), .f(decodificador_hexa_3_f), .a(decodificador_hexa_3_a),
    .b(decodificador_hexa_3_b), .e(decodificador_hexa_3_e), .d(decodificador_hexa_3_d),
    .c(decodificador_hexa_3_c));  // open: dp

  // Notes on the sheet:
  //   ALUNO: Arthur de Sá Braz de Matos
  //   MATRÍCULA: 801778
  //   Somador
  //   Decod. Y
  //   Decod. X
  //   Decod. Resul.
endmodule

module ULA_1bit (
  input  A,
  input  op1,
  input  op0,
  input  B_invert,
  input  c_in,
  input  B,
  output s,
  output c_out
);

  wire and_1_out, multiplexer_1_out, not_1_out, not_2_out, or_1_out, somadorcompleto2bits_1_s;

  not not_1 (not_1_out, B);
  Multiplexer #(.enable("false")) multiplexer_1 (.in0(B), .in1(not_1_out), .out(multiplexer_1_out), .sel(B_invert));
  and and_1 (and_1_out, A, multiplexer_1_out);
  or or_1 (or_1_out, A, multiplexer_1_out);
  not not_2 (not_2_out, A);
  somadorCompleto2Bits somadorcompleto2bits_1 (
    .X(A), .Vem1(c_in), .Y(multiplexer_1_out), .Vai1(c_out), .S(somadorcompleto2bits_1_s));
  MUX mux_1 (.m(and_1_out), .n(or_1_out), .o(not_2_out), .p(somadorcompleto2bits_1_s), .op1(op1), .op0(op0), .s_mux(s));
endmodule

module MUX (
  input  m,
  input  n,
  input  o,
  input  p,
  input  op1,
  input  op0,
  output s_mux
);

  wire and_1_out, and_2_out, and_3_out, and_4_out, not_1_out, not_2_out, not_3_out, not_4_out;

  and and_1 (and_1_out, m, not_1_out, not_2_out);
  not not_1 (not_1_out, op1);
  not not_2 (not_2_out, op0);
  and and_2 (and_2_out, n, not_3_out, op0);
  not not_3 (not_3_out, op1);
  and and_3 (and_3_out, o, op1, not_4_out);
  not not_4 (not_4_out, op0);
  and and_4 (and_4_out, p, op1, op0);
  or or_1 (s_mux, and_1_out, and_2_out, and_3_out, and_4_out);
endmodule

module ULA_4bit (
  input  B_invert,
  input  op1,
  input  op0,
  input  a3,
  input  a2,
  input  a1,
  input  a0,
  input  b3,
  input  b2,
  input  b1,
  input  b0,
  output s0,
  output s1,
  output s2,
  output s3,
  output c_out
);

  wire ula_1bit_1_c_out, ula_1bit_2_c_out, ula_1bit_3_c_out;

  ULA_1bit ula_1bit_1 (
    .A(a0), .B(b0), .B_invert(B_invert), .c_in(B_invert), .c_out(ula_1bit_1_c_out), .op1(op1), .op0(op0),
    .s(s0));
  ULA_1bit ula_1bit_2 (
    .A(a1), .B(b1), .B_invert(B_invert), .c_in(ula_1bit_1_c_out), .c_out(ula_1bit_2_c_out), .op1(op1),
    .op0(op0), .s(s1));
  ULA_1bit ula_1bit_3 (
    .A(a2), .B(b2), .B_invert(B_invert), .c_in(ula_1bit_2_c_out), .c_out(ula_1bit_3_c_out), .op1(op1),
    .op0(op0), .s(s2));
  ULA_1bit ula_1bit_4 (
    .A(a3), .B(b3), .B_invert(B_invert), .c_in(ula_1bit_3_c_out), .c_out(c_out), .op1(op1), .op0(op0), .s(s3));
endmodule
