// Logisim project EP02_pt2.circ as structural Verilog: 2 circuits, main circuit ULA_4_bits
module ULA_4_bits (
  input  [3:0] a,
  input  [3:0] b,
  input  [3:0] opCode,
  output [3:0] saida
);

  wire [3:0] and_1_out, and_2_out, and_3_out, nand_1_out, nand_2_out, not_1_out, not_2_out, or_1_out,
       or_2_out, or_3_out, xor_1_out, xor_2_out;

  assign not_1_out = ~a;  // NOT_Gate not_1, 4 bits wide
  assign not_2_out = ~b;  // NOT_Gate not_2, 4 bits wide
  assign nand_1_out = ~(not_1_out & b);  // NAND_Gate nand_1, 4 bits wide
  assign nand_2_out = ~(a & b);  // NAND_Gate nand_2, 4 bits wide
  assign and_1_out = not_1_out & b;  // AND_Gate and_1, 4 bits wide
  assign xor_1_out = a ^ b;  // XOR_Gate xor_1, 4 bits wide
  assign and_2_out = a & not_2_out;  // AND_Gate and_2, 4 bits wide
  assign or_1_out = not_1_out | not_2_out;  // OR_Gate or_1, 4 bits wide
  assign xor_2_out = not_1_out ^ not_2_out;  // XOR_Gate xor_2, 4 bits wide
  assign and_3_out = a & b;  // AND_Gate and_3, 4 bits wide
  assign or_2_out = a | not_2_out;  // OR_Gate or_2, 4 bits wide
  assign or_3_out = a | b;  // OR_Gate or_3, 4 bits wide
  Multiplexer #(.select(4), .width(4), .enable("false")) multiplexer_1 (
    .in0(not_2_out), .in1(nand_1_out), .in2(and_1_out), .in3(4'b0000), .in4(nand_2_out), .in5(not_1_out),
    .in6(xor_1_out), .in7(and_2_out), .in8(or_1_out), .in9(xor_2_out), .in10(b), .in11(and_3_out),
    .in12(4'b1111), .in13(or_2_out), .in14(or_3_out), .in15(a), .out(saida), .sel(opCode));
endmodule

module ULA_1_bit (
  input  a,
  input  b,
  input  s,
  output f
);

  wire nor_1_out, not_1_out;

  not not_1 (not_1_out, a);
  nor nor_1 (nor_1_out, a, b);
  Multiplexer #(.enable("false")) multiplexer_1 (.in0(not_1_out), .in1(nor_1_out), .out(f), .sel(s));
endmodule
